# Fritzing sketch Digital_7segment_control (saved by Fritzing 0.9.3b)
breadboards: 1

parts:
  Composant1 = Arduino Nano (Rev3.0)
  U1 = 74HC595 SMD [package="SO16 [SMD]"]
  7_Segment2 = 7 Segment Display
  7_Segment1 = 7 Segment Display
  Q1 = NPN-Transistor [package="TO92 [THT]"]
  Q2 = NPN-Transistor [package="TO92 [THT]"]
  R1 = Resistor [tolerance=±5% resistance=220 package=THT]
  R2 = Resistor [tolerance=±5% resistance=220 package=THT]

nets:
  GND: Composant1.GND, U1.GND, U1.OE, Q1.E, Q2.E
  N1: Composant1.D2, U1.DS
  N2: Composant1.D3, U1.SH_CP
  N3: Composant1.D4, U1.ST_CP
  N4: Composant1.D5, R1.Pin_0
  N5: Composant1.D6, R2.Pin_0
  N6: Composant1.D13/SCK, U1.MR, U1.VCC
  N7: U1.Q1, 7_Segment2.Segment_B, 7_Segment1.Segment_B
  N8: U1.Q2, 7_Segment2.Segment_C, 7_Segment1.Segment_C
  N9: U1.Q3, 7_Segment2.Segment_D, 7_Segment1.Segment_D
  N10: U1.Q4, 7_Segment2.Segment_E, 7_Segment1.Segment_E
  N11: U1.Q5, 7_Segment2.Segment_G, 7_Segment1.Segment_G
  N12: U1.Q6, 7_Segment2.Segment_F, 7_Segment1.Segment_F
  N13: U1.Q7, 7_Segment2.Segment_DP, 7_Segment1.Segment_DP
  N14: U1.Q0, 7_Segment2.Segment_A, 7_Segment1.Segment_A
  N15: 7_Segment2.common_cathode, Q2.C
  N16: 7_Segment1.common_cathode, Q1.C
  N17: Q1.B, R2.Pin_1
  N18: Q2.B, R1.Pin_1

notes:
  latch
  data
  clock
  3v3 voltage
